# Fritzing sketch Safe 5LED (saved by Fritzing 0.9.3b)
breadboards: 1

parts:
  J21_Header_on_Jetson_TX1 = double row female pin header, 20 pins [form="♀ (female)"]
  J21_Evens = double row female pin header, 20 pins [form="♀ (female)"]
  R1 = Resistor [tolerance=±5% resistance=330 package="1206 [SMD]"]
  R2 = Resistor [tolerance=±5% resistance=330 package="1206 [SMD]"]
  R3 = Resistor [tolerance=±5% resistance=330 package="1206 [SMD]"]
  R4 = Resistor [tolerance=±5% resistance=330 package="1206 [SMD]"]
  R5 = Resistor [tolerance=±5% resistance=330 package="1206 [SMD]"]
  R6 = Resistor [tolerance=±5% resistance=10k package="1206 [SMD]"]
  R7 = Resistor [tolerance=±5% resistance=10k package="1206 [SMD]"]
  R8 = Resistor [tolerance=±5% resistance=10k package="1206 [SMD]"]
  R9 = Resistor [tolerance=±5% resistance=10k package="1206 [SMD]"]
  R10 = Resistor [tolerance=±5% resistance=10k package="1206 [SMD]"]
  NPN5 = NPN-Transistor [part_number="2N3904 or BC547 NPN" package="TO92 [THT]"]
  LED1 = LED - 3mm [color="Red (633nm)" package="3 mm [THT]"]
  NPN2 = NPN-Transistor [part_number="2N3904 or BC547" package="TO92 [THT]"]
  NPN3 = NPN-Transistor [part_number="2N3904 or BC547" package="TO92 [THT]"]
  NPN4 = NPN-Transistor [part_number="2N3904 or BC547" package="TO92 [THT]"]
  NPN5_2 = NPN-Transistor [part_number="2N3904 or BC547" package="TO92 [THT]"]
  LED2 = LED - 3mm [color="Red (633nm)" package="3 mm [THT]"]
  LED3 = LED - 3mm [color="Red (633nm)" package="3 mm [THT]"]
  LED4 = LED - 3mm [color="Red (633nm)" package="3 mm [THT]"]
  2_3V_LED = LED - 3mm [color="Red (633nm)" package="3 mm [THT]"]

nets:
  N1: J21_Header_on_Jetson_TX1.pin7, R6.Pin_0
  N2: J21_Header_on_Jetson_TX1.pin15, R9.Pin_0
  N3: J21_Header_on_Jetson_TX1.pin17, R10.Pin_0
  N4: J21_Evens.pin2, R1.Pin_1, R2.Pin_1, R3.Pin_1, R4.Pin_1, R5.Pin_1
  N5: J21_Evens.pin3, NPN5.E, NPN2.E, NPN3.E, NPN4.E, NPN5_2.E
  N6: J21_Evens.pin8, R7.Pin_0
  N7: J21_Evens.pin9, R8.Pin_0
  N8: R1.Pin_0, LED1.anode
  N9: R2.Pin_0, LED2.anode
  N10: R3.Pin_0, LED3.anode
  N11: R4.Pin_0, LED4.anode
  N12: R5.Pin_0, 2_3V_LED.anode
  N13: R6.Pin_1, NPN5.B
  N14: R7.Pin_1, NPN2.B
  N15: R8.Pin_1, NPN3.B
  N16: R9.Pin_1, NPN4.B
  N17: R10.Pin_1, NPN5_2.B
  N18: NPN5.C, LED1.cathode
  N19: NPN2.C, LED2.cathode
  N20: NPN3.C, LED3.cathode
  N21: NPN4.C, LED4.cathode
  N22: NPN5_2.C, 2_3V_LED.cathode

notes:
  Red: Pin 4, 5V
  Black: Pin 6, GND
  Purple: Pin 13, gpio38
  Blue: Pin 16, gpio37
  Green: Pin 18, gpio184
  Yellow: Pin 29, gpio219
  Orange: Pin 33, gpio63
  Class 0
  Class 1
  Class 2
  Class 3
  Class 4
  NPN Transistor Connections:
  Emitter: GND
  Base: 10KΩ Resistor
  Collector: LED Cathode
  LED Connections:
  Cathode: NPN Collector
  Anode: 330Ω Resistor
